// Logisim project Mearly.circ as structural Verilog: 1 circuit, main circuit main
module main (
  input  ADDR,
  input  R_W,
  input  in_3,
  input  in_4,
  input  in_5,
  input  in_6,
  input  SET,
  input  CLR,
  output out_9,
  output out_10,
  output out_11,
  output out_12
);

  wire and_1_out, clock_1_out;

  Clock clock_1 (.out(clock_1_out));
  and and_1 (and_1_out, ADDR, clock_1_out);
  J_K_Flip_Flop j_k_ff_1 (.J(in_3), .clk(and_1_out), .K(SET), .Q(out_9), .reset(CLR));  // open: Qn, preset
  J_K_Flip_Flop j_k_ff_2 (.J(in_4), .clk(and_1_out), .K(SET), .Q(out_10), .reset(CLR));  // open: Qn, preset
  J_K_Flip_Flop j_k_ff_3 (.J(in_5), .clk(and_1_out), .K(SET), .Q(out_11), .reset(CLR));  // open: Qn, preset
  J_K_Flip_Flop j_k_ff_4 (.J(in_6), .clk(and_1_out), .K(SET), .Q(out_12), .reset(CLR));  // open: Qn, preset
endmodule
