// Logisim project Q_01a.circ as structural Verilog: 1 circuit, main circuit main
module main (
  input  a,
  input  b,
  input  c,
  input  d,
  output out_5
);

  wire and_1_out, and_2_out, and_3_out, and_4_out, and_5_out, and_6_out, and_7_out, and_8_out, and_9_out,
       and_10_out, not_1_out, not_2_out, not_3_out, not_4_out, or_1_out, or_3_out;

  not not_1 (not_1_out, c);
  not not_2 (not_2_out, a);
  not not_3 (not_3_out, d);
  not not_4 (not_4_out, b);
  and and_1 (and_1_out, a, b);
  and and_2 (and_2_out, not_1_out, d);
  and and_3 (and_3_out, not_2_out, b);
  and and_4 (and_4_out, c, d);
  and and_5 (and_5_out, c, not_3_out);
  and and_6 (and_6_out, a, not_4_out);
  and and_7 (and_7_out, and_1_out, and_2_out);
  and and_8 (and_8_out, and_3_out, and_4_out);
  and and_9 (and_9_out, a, and_5_out);
  and and_10 (and_10_out, and_6_out, c);
  or or_1 (or_1_out, and_7_out, and_8_out);
  or or_2 (out_5, or_1_out, or_3_out);
  or or_3 (or_3_out, and_9_out, and_10_out);
endmodule
