// Logisim project Q_01c.circ as structural Verilog: 1 circuit, main circuit main
module main (
  input  a,
  input  b,
  input  c,
  input  d,
  output out_5
);

  wire and_1_out, and_2_out, and_3_out, and_4_out, and_5_out, and_6_out, not_1_out, not_2_out, not_3_out,
       not_4_out, or_1_out, or_3_out;

  not not_1 (not_1_out, c);
  not not_2 (not_2_out, c);
  not not_3 (not_3_out, a);
  not not_4 (not_4_out, b);
  and and_1 (and_1_out, not_1_out, d);
  and and_2 (and_2_out, not_2_out, d);
  and and_3 (and_3_out, c, d);
  and and_4 (and_4_out, c, d);
  and and_5 (and_5_out, not_3_out, and_3_out);
  and and_6 (and_6_out, not_4_out, and_4_out);
  or or_1 (or_1_out, and_1_out, and_2_out);
  or or_2 (out_5, or_1_out, or_3_out);
  or or_3 (or_3_out, and_5_out, and_6_out);
endmodule
