// Logisim project Q_01d.circ as structural Verilog: 1 circuit, main circuit main
module main (
  input  a,
  input  b,
  input  c,
  input  d,
  output out_5
);

  wire and_1_out, and_2_out, and_3_out, and_4_out, not_1_out, not_2_out;

  not not_1 (not_1_out, c);
  not not_2 (not_2_out, d);
  and and_1 (and_1_out, c, d);
  and and_2 (and_2_out, not_1_out, not_2_out);
  and and_3 (and_3_out, b, and_1_out);
  and and_4 (and_4_out, a, and_2_out);
  or or_1 (out_5, and_3_out, and_4_out);
endmodule
