// Logisim project Q_01f.circ as structural Verilog: 1 circuit, main circuit main
module main (
  input  a,
  input  b,
  input  c,
  input  d,
  output out_5
);

  wire and_1_out, and_2_out, and_3_out, and_4_out, not_1_out;

  not not_1 (not_1_out, c);
  and and_1 (and_1_out, a, b);
  and and_2 (and_2_out, c, d);
  and and_3 (and_3_out, d, not_1_out);
  and and_4 (and_4_out, and_1_out, and_2_out);
  or or_1 (out_5, and_3_out, and_4_out);
endmodule
