// Logisim project Q_03.circ as structural Verilog: 1 circuit, main circuit main
module main (
  input  in_1,
  input  CLR
);

  wire a_qn, b_qn, clock_1_out;

  Clock clock_1 (.out(clock_1_out));
  J_K_Flip_Flop a (.J(in_1), .clk(clock_1_out), .K(in_1), .Qn(a_qn), .reset(CLR));  // open: Q, preset
  J_K_Flip_Flop b (.J(a_qn), .clk(clock_1_out), .K(a_qn), .Qn(b_qn), .reset(CLR));  // open: Q, preset
  J_K_Flip_Flop c (.J(b_qn), .clk(clock_1_out), .K(b_qn), .reset(CLR));  // open: Q, Qn, preset
endmodule
