// Logisim project Q_04.circ as structural Verilog: 1 circuit, main circuit main
module main (
  input  in_1,
  input  CLR
);

  wire a_q, b_qn, clock_1_out, d_ff_1_q, d_ff_1_qn;

  Clock clock_1 (.out(clock_1_out));
  D_Flip_Flop a (.clk(clock_1_out), .D(in_1), .Q(a_q), .reset(CLR));  // open: Qn, preset
  D_Flip_Flop b (.clk(clock_1_out), .D(a_q), .Qn(b_qn), .reset(CLR));  // open: Q, preset
  D_Flip_Flop d_ff_1 (.clk(clock_1_out), .D(b_qn), .Q(d_ff_1_q), .Qn(d_ff_1_qn), .reset(CLR));  // open: preset
endmodule
