// Logisim project TP2.circ as structural Verilog: 2 circuits, main circuit main
module main (
  input  [1:0] OP,
  input  B3,
  input  B2,
  input  B1,
  input  B0,
  input  A3,
  input  A2,
  input  A1,
  input  A0,
  input  Binvert,
  output S0,
  output S1,
  output S2,
  output S3,
  output Cout
);

  wire ULA0_cout, ULA1_cout, ULA2_cout;

  ULA ULA0 (.a(A0), .b(B0), .Binverter(Binvert), .in_1(Binvert), .Cout(ULA0_cout), .in_5(OP), .S(S0));
  ULA ULA1 (.a(A1), .b(B1), .Binverter(Binvert), .in_1(ULA0_cout), .Cout(ULA1_cout), .in_5(OP), .S(S1));
  ULA ULA2 (.a(A2), .b(B2), .Binverter(Binvert), .in_1(ULA1_cout), .Cout(ULA2_cout), .in_5(OP), .S(S2));
  ULA ULA3 (.a(A3), .b(B3), .Binverter(Binvert), .in_1(ULA2_cout), .Cout(Cout), .in_5(OP), .S(S3));

  // Notes on the sheet:
  //   Cin
endmodule

module ULA (
  input  in_1,
  input  Binverter,
  input  a,
  input  b,
  input  [1:0] in_5,
  output S,
  output Cout
);

  wire adder_1_out, and_1_out, multiplexer_1_out, not_1_out, not_2_out, or_1_out;

  not not_1 (not_1_out, b);
  Multiplexer #(.enable("false")) multiplexer_1 (.in0(b), .in1(not_1_out), .out(multiplexer_1_out), .sel(Binverter));
  and and_1 (and_1_out, a, multiplexer_1_out);
  or or_1 (or_1_out, a, multiplexer_1_out);
  not not_2 (not_2_out, a);
  Adder #(.width(1)) adder_1 (.a(a), .b(multiplexer_1_out), .out(adder_1_out), .cin(in_1), .cout(Cout));
  Multiplexer #(.select(2), .enable("false")) multiplexer_2 (
    .in0(and_1_out), .in1(or_1_out), .in2(not_2_out), .in3(adder_1_out), .out(S), .sel(in_5));
endmodule
