// Logisim project circ.circ as structural Verilog: 1 circuit, main circuit main
module main (
  input  [3:0] A,
  input  [3:0] B,
  input  [3:0] S0_S1_S2_S3,
  output [3:0] F0_F1_F2_F3
);

  wire [3:0] and_1_out, and_2_out, and_3_out, and_4_out, not_1_out, not_2_out, not_3_out, not_4_out,
       not_5_out, or_1_out, or_2_out, or_3_out, or_4_out, xor_1_out, xor_2_out;

  assign not_1_out = ~A;  // NOT_Gate not_1, 4 bits wide
  assign not_2_out = ~B;  // NOT_Gate not_2, 4 bits wide
  assign or_1_out = A | B;  // OR_Gate or_1, 4 bits wide
  assign not_3_out = ~or_1_out;  // NOT_Gate not_3, 4 bits wide
  assign and_1_out = not_1_out & B;  // AND_Gate and_1, 4 bits wide
  assign not_4_out = ~and_2_out;  // NOT_Gate not_4, 4 bits wide
  assign and_2_out = A & B;  // AND_Gate and_2, 4 bits wide
  assign xor_1_out = B ^ A;  // XOR_Gate xor_1, 4 bits wide
  assign and_3_out = A & not_2_out;  // AND_Gate and_3, 4 bits wide
  assign or_2_out = not_1_out | B;  // OR_Gate or_2, 4 bits wide
  assign xor_2_out = A ^ B;  // XOR_Gate xor_2, 4 bits wide
  assign not_5_out = ~xor_2_out;  // NOT_Gate not_5, 4 bits wide
  assign and_4_out = A & B;  // AND_Gate and_4, 4 bits wide
  assign or_3_out = A | not_2_out;  // OR_Gate or_3, 4 bits wide
  assign or_4_out = A | B;  // OR_Gate or_4, 4 bits wide
  Multiplexer #(.select(4), .width(4), .enable("false")) multiplexer_1 (
    .in0(not_1_out), .in1(not_3_out), .in2(and_1_out), .in3(4'b0000), .in4(not_4_out), .in5(not_2_out),
    .in6(xor_1_out), .in7(and_3_out), .in8(or_2_out), .in9(not_5_out), .in10(B), .in11(and_4_out),
    .in12(4'b0001), .in13(or_3_out), .in14(or_4_out), .in15(A), .out(F0_F1_F2_F3), .sel(S0_S1_S2_S3));
endmodule
